# Fritzing sketch crossover (saved by Fritzing 0.9.2b)
breadboards: 1

parts:
  C16A = Electrolytic Capacitor [capacitance=15.6µF package="100 mil [THT, electrolytic]"]
  C16B = Electrolytic Capacitor [capacitance=25µF package="100 mil [THT, electrolytic]"]
  L2 = Inductor [inductance=1.6mH package="1206 [SMD]"]
  L3 = Inductor [inductance=2.6mH package="1206 [SMD]"]
  Jin = 3.5mm Audio Jack [package=audio-jack-3.5mm-smd]
  Jhi = 3.5mm Audio Jack [package=audio-jack-3.5mm-smd]
  Jlo = 3.5mm Audio Jack [package=audio-jack-3.5mm-smd]

nets:
  N1: C16A.-, C16B.+, Jin.SLEEVE, Jlo.LEFT
  N2: C16A.+, L2.pin_1, Jhi.LEFT
  N3: C16B.-, L3.pin_1, Jlo.SLEEVE
  N4: L2.pin_0, L3.pin_0, Jin.LEFT, Jhi.SLEEVE

notes:
  mini-leslie crossover, https://github.com/dizzib/mini-leslie, 0.1
